// Logisim project BIP.circ as structural Verilog: 1 circuit, main circuit main
module main (
  output [15:0] out_1
);

  wire CLOCK_out, undriven, undriven_2, undriven_3, undriven_4, undriven_5, undriven_6, undriven_7;
  wire [15:0] adder_1_out, adder_2_out, and_1_out, and_2_out, demultiplexer_1_out0, demultiplexer_1_out1,
       demultiplexer_2_out0, demultiplexer_2_out1, IR_q, multiplexer_1_out, multiplexer_3_out, PC_q,
       ram_1_data, ram_2_data, subtractor_1_out;

  Clock CLOCK (.out(CLOCK_out));
  assign and_1_out = PC_q & {16{1'b1}};  // AND_Gate and_1, 16 bits wide
  Adder #(.width(16)) adder_1 (.a(and_1_out), .b(16'h1), .out(adder_1_out));  // open: cin, cout
  Register #(.width(16)) PC (.D(adder_1_out), .en(undriven), .Q(PC_q), .clk(CLOCK_out));  // open: clr
  RAM #(.addrWidth(16), .dataWidth(16)) ram_1 (
    .addr(and_2_out), .data(ram_1_data), .sel(undriven_2), .clk(CLOCK_out), .ld(undriven_3));  // open: clr
  Multiplexer #(.width(16)) multiplexer_1 (
    .in0(ram_1_data), .in1(and_2_out), .out(multiplexer_1_out), .en(undriven_4));  // open: sel
  Demultiplexer #(.width(16)) demultiplexer_1 (
    .out0(demultiplexer_1_out0), .out1(demultiplexer_1_out1), .in(multiplexer_1_out), .en(undriven_5));  // open: sel
  RAM #(.addrWidth(16), .dataWidth(16)) ram_2 (.addr(PC_q), .data(ram_2_data), .sel(1'b1));  // open: clk, ld, clr
  Register #(.width(16)) IR (.D(ram_2_data), .en(1'b1), .Q(IR_q), .clk(CLOCK_out));  // open: clr
  Adder #(.width(16)) adder_2 (
    .a(demultiplexer_2_out0), .b(demultiplexer_1_out0), .out(adder_2_out));  // open: cin, cout
  Multiplexer #(.select(2), .width(16)) multiplexer_2 (
    .in1(adder_2_out), .in3(subtractor_1_out), .out(out_1));  // open: in0, in2, sel, en
  assign and_2_out = IR_q & {16{1'b1}};  // AND_Gate and_2, 16 bits wide
  Multiplexer #(.select(2), .width(16)) multiplexer_3 (
    .in0(ram_1_data), .in1(and_2_out), .in2(out_1), .out(multiplexer_3_out), .en(undriven_6));  // open: in3, sel
  Register #(.width(16)) ACC (.D(multiplexer_3_out), .Q(ram_1_data), .clk(CLOCK_out));  // open: en, clr
  Demultiplexer #(.width(16)) demultiplexer_2 (
    .out0(demultiplexer_2_out0), .out1(demultiplexer_2_out1), .in(ram_1_data), .en(undriven_7));  // open: sel
  Subtractor #(.width(16)) subtractor_1 (
    .a(demultiplexer_1_out1), .b(demultiplexer_2_out1), .out(subtractor_1_out));  // open: bin, bout
endmodule
