// Logisim project Programa1.circ as structural Verilog: 1 circuit, main circuit main
module main (
  output [11:0] NEXT,
  output [11:0] ADD,
  output [15:0] INSCTRUCTION
);

  wire clock_1_out;
  wire [15:0] rom_1_data;

  Clock clock_1 (.out(clock_1_out));
  Register #(.width(12)) PC (.D(NEXT), .Q(ADD), .clk(clock_1_out));  // open: en, clr
  ROM #(.addrWidth(12), .dataWidth(16)) rom_1 (.addr(ADD), .data(rom_1_data), .sel(1'b1));
  Adder #(.width(12)) adder_1 (.a(ADD), .b(12'h1), .out(NEXT));  // open: cin, cout
  Register #(.width(16)) IR (.D(rom_1_data), .Q(INSCTRUCTION), .clk(clock_1_out));  // open: en, clr

  // Notes on the sheet:
  //   contents of rom_1 (hex, n*v repeats v):
  //   1212 343 5454
endmodule
