// Logisim project Só_logicadecontrole.circ as structural Verilog: 11 circuits, main circuit main
module main (
  output [15:0] out_1
);

  wire clock_out, logica_de_controle_1_en_pc, logica_de_controle_1_en_ram, logica_de_controle_1_sel_ula,
       logica_de_controle_1_selop2, logica_de_controle_1_sto;
  wire [1:0] logica_de_controle_1_out_9;
  wire [15:0] caminho_de_controle_1_out_3;

  Clock clock (.out(clock_out));
  Logica_de_Controle logica_de_controle_1 (
    .EN_RAM(logica_de_controle_1_en_ram), .STO(logica_de_controle_1_sto),
    .SEL_ULA(logica_de_controle_1_sel_ula), .A(1'b0), .B(1'b1), .C(1'b1), .D(1'b1),
    .out_9(logica_de_controle_1_out_9), .En_PC(logica_de_controle_1_en_pc),
    .selop2(logica_de_controle_1_selop2));  // open: WR_ACC
  Caminho_de_Controle caminho_de_controle_1 (
    .out_3(caminho_de_controle_1_out_3), .En_PC(logica_de_controle_1_en_ram), .Clock(clock_out));
  Caminho_de_Dados caminho_de_dados_1 (
    .in_1(caminho_de_controle_1_out_3), .En_RAM(logica_de_controle_1_en_pc), .STO(logica_de_controle_1_sto),
    .SEL_OP2(logica_de_controle_1_selop2), .DEMUX1(logica_de_controle_1_sel_ula),
    .SEL_OP1(logica_de_controle_1_out_9), .DEMUX2(logica_de_controle_1_sel_ula), .out_9(out_1),
    .Clock(clock_out));
endmodule

module EN_ROM (
  input  D,
  input  C,
  input  B,
  input  A,
  output out_5
);

  wire and_1_out, and_2_out, and_3_out, not_1_out;

  not not_1 (not_1_out, A);
  and and_1 (and_1_out, B, not_1_out);
  and and_2 (and_2_out, not_1_out, C);
  and and_3 (and_3_out, D, not_1_out);
  or or_1 (out_5, and_1_out, and_2_out, and_3_out);
endmodule

module EN_RAM (
  input  A,
  input  B,
  input  C,
  input  D,
  output out_5
);

  wire and_1_out, and_2_out, and_3_out, not_1_out, not_2_out, not_3_out, not_4_out;

  not not_1 (not_1_out, A);
  not not_2 (not_2_out, B);
  not not_3 (not_3_out, C);
  not not_4 (not_4_out, D);
  and and_1 (and_1_out, not_1_out, B, not_4_out);
  and and_2 (and_2_out, not_1_out, not_4_out, C);
  and and_3 (and_3_out, not_1_out, not_2_out, not_3_out, D);
  or or_1 (out_5, and_1_out, and_3_out, and_2_out);
endmodule

module WR_RAM (
  input  A,
  input  B,
  input  C,
  input  D,
  output out_5
);

  wire not_1_out, not_2_out, not_3_out;

  not not_1 (not_1_out, A);
  not not_2 (not_2_out, B);
  not not_3 (not_3_out, C);
  and and_1 (out_5, not_1_out, not_2_out, not_3_out, D);
endmodule

module Logica_de_Controle (
  input  A,
  input  B,
  input  C,
  input  D,
  output En_PC,
  output EN_RAM,
  output STO,
  output WR_ACC,
  output [1:0] out_9,
  output SEL_ULA,
  output selop2
);

  wire sel_op_1_1_sel_op_bit0, sel_op_1_1_sel_op_bit_1;

  not not_1 (En_PC, A);
  EN_ROM en_rom_1 ();  // open: D, C, B, A, out_5
  EN_RAM en_ram_1 (.A(A), .B(B), .C(C), .D(D), .out_5(EN_RAM));
  WR_RAM wr_ram_1 (.out_5(STO), .A(A), .B(B), .C(C), .D(D));
  WR_ACC wr_acc_1 (.out_5(WR_ACC), .A(A), .B(B), .C(C), .D(D));
  SEL_ULA sel_ula_1 (.out_5(SEL_ULA), .A(A), .B(B), .C(C), .D(D));
  SEL_OP2 u_SELOP2 (.out_5(selop2), .A(A), .B(B), .C(C), .D(D));
  SEL_OP_1 sel_op_1_1 (
    .SEL_OP_BIT_1(sel_op_1_1_sel_op_bit_1), .SEL_OP_BIT0(sel_op_1_1_sel_op_bit0), .in_1(A), .in_2(B),
    .in_3(C), .in_4(D));
  assign out_9 = {{1{sel_op_1_1_sel_op_bit_1}}, sel_op_1_1_sel_op_bit0};  // Bit_Extender bit_extender_1

  // Notes on the sheet:
  //   Bit1
  //   Bit0
endmodule

module WR_ACC (
  input  A,
  input  B,
  input  C,
  input  D,
  output out_5
);

  wire and_1_out, and_2_out, not_1_out;

  not not_1 (not_1_out, A);
  and and_1 (and_1_out, not_1_out, B);
  and and_2 (and_2_out, not_1_out, C);
  or or_1 (out_5, and_1_out, and_2_out);
  // also tied to GND on the sheet: D
endmodule

module SEL_OP_1 (
  input  in_1,
  input  in_2,
  input  in_3,
  input  in_4,
  output SEL_OP_BIT_1,
  output SEL_OP_BIT0
);

  wire not_1_out, not_2_out;

  not not_1 (not_1_out, in_1);
  not not_2 (not_2_out, in_2);
  and and_1 (SEL_OP_BIT_1, not_1_out, in_2);
  and and_2 (SEL_OP_BIT0, not_1_out, not_2_out, in_3, in_4);
endmodule

module SEL_ULA (
  input  A,
  input  B,
  input  C,
  input  D,
  output out_5
);

  wire not_1_out, not_2_out;

  not not_1 (not_1_out, D);
  not not_2 (not_2_out, A);
  and and_1 (out_5, not_2_out, B, C, not_1_out);
endmodule

module SEL_OP2 (
  input  A,
  input  B,
  input  C,
  input  D,
  output out_5
);

  wire and_1_out, and_2_out, not_1_out;

  not not_1 (not_1_out, A);
  and and_1 (and_1_out, not_1_out, C, D);
  and and_2 (and_2_out, not_1_out, B, D);
  or or_1 (out_5, and_1_out, and_2_out);
endmodule

module Caminho_de_Dados (
  input  [15:0] in_1,
  input  Clock,
  input  En_RAM,
  input  STO,
  input  SEL_OP2,
  input  DEMUX1,
  input  [1:0] SEL_OP1,
  input  DEMUX2,
  output [15:0] out_9
);

  wire bit_extender_1_out;
  wire [15:0] adder_1_out, and_1_out, demultiplexer_1_out0, demultiplexer_1_out1, demultiplexer_2_out0,
       demultiplexer_2_out1, multiplexer_1_out, multiplexer_3_out, ram_1_data, subtractor_1_out;

  RAM #(.addrWidth(16), .dataWidth(16)) ram_1 (
    .addr(and_1_out), .data(ram_1_data), .sel(En_RAM), .clk(Clock), .ld(STO));  // open: clr
  Bit_Extender #(.in_width(2), .out_width(1), .\type ("sign")) bit_extender_1 (.in(SEL_OP1), .out(bit_extender_1_out));
  Multiplexer #(.width(16)) multiplexer_1 (
    .in0(ram_1_data), .in1(and_1_out), .out(multiplexer_1_out), .en(SEL_OP2));  // open: sel
  Demultiplexer #(.width(16)) demultiplexer_1 (
    .out0(demultiplexer_1_out0), .out1(demultiplexer_1_out1), .in(multiplexer_1_out), .en(DEMUX1));  // open: sel
  Adder #(.width(16)) adder_1 (
    .a(demultiplexer_2_out0), .b(demultiplexer_1_out0), .out(adder_1_out));  // open: cin, cout
  Multiplexer #(.select(2), .width(16), .enable("false")) multiplexer_2 (
    .in0(adder_1_out), .in1(subtractor_1_out), .out(out_9));  // open: in2, in3, sel
  assign and_1_out = in_1 & {16{1'b1}};  // AND_Gate and_1, 16 bits wide
  Multiplexer #(.select(2), .width(16)) multiplexer_3 (
    .in0(ram_1_data), .in1(and_1_out), .in2(out_9), .out(multiplexer_3_out), .en(bit_extender_1_out));  // open: in3, sel
  Register #(.width(16)) ACC (.D(multiplexer_3_out), .Q(ram_1_data), .clk(Clock));  // open: en, clr
  Demultiplexer #(.width(16)) demultiplexer_2 (
    .out0(demultiplexer_2_out0), .out1(demultiplexer_2_out1), .in(ram_1_data), .en(DEMUX2));  // open: sel
  Subtractor #(.width(16)) subtractor_1 (
    .a(demultiplexer_1_out1), .b(demultiplexer_2_out1), .out(subtractor_1_out));  // open: bin, bout

  // Notes on the sheet:
  //   IR_OUT
endmodule

module Caminho_de_Controle (
  input  Clock,
  input  En_PC,
  output [15:0] out_3
);

  wire [15:0] adder_1_out, and_1_out, PC_q, ram_1_data;

  assign and_1_out = PC_q & {16{1'b1}};  // AND_Gate and_1, 16 bits wide
  Adder #(.width(16)) adder_1 (.a(and_1_out), .b(16'h2), .out(adder_1_out));  // open: cin, cout
  Register #(.width(16)) PC (.D(adder_1_out), .en(En_PC), .Q(PC_q), .clk(Clock));  // open: clr
  RAM #(.addrWidth(16), .dataWidth(16)) ram_1 (.addr(PC_q), .data(ram_1_data), .sel(1'b1));  // open: clk, ld, clr
  Register #(.width(16)) IR (.D(ram_1_data), .en(1'b1), .Q(out_3), .clk(Clock));  // open: clr
endmodule
