// Logisim project Trabalho_COMPLETO_.circ as structural Verilog: 11 circuits, main circuit main
module main (
  output [15:0] out_1
);

  wire button_1_out, button_2_out, clock_out, logica_de_controle_1_en_pc, logica_de_controle_1_en_ram,
       logica_de_controle_1_sel_op2, logica_de_controle_1_ula_demux2, logica_de_controle_1_wr_acc,
       logica_de_controle_1_wr_ram;
  wire [1:0] logica_de_controle_1_sel_op1;
  wire [15:0] caminho_de_controle_1_out_4, caminho_de_controle_1_out_5;

  Logica_de_Controle logica_de_controle_1 (
    .WR_RAM(logica_de_controle_1_wr_ram), .EN_RAM(logica_de_controle_1_en_ram),
    .WR_ACC(logica_de_controle_1_wr_acc), .SEL_OP1(logica_de_controle_1_sel_op1),
    .SEL_OP2(logica_de_controle_1_sel_op2), .ULA_DEMUX2(logica_de_controle_1_ula_demux2),
    .EN_PC(logica_de_controle_1_en_pc), .in_1(caminho_de_controle_1_out_4));
  Clock clock (.out(clock_out));
  Button button_1 (.out(button_1_out));
  Caminho_de_Controle caminho_de_controle_1 (
    .Clock(clock_out), .En_PC(logica_de_controle_1_en_pc), .CLR(button_1_out),
    .out_4(caminho_de_controle_1_out_4), .out_5(caminho_de_controle_1_out_5));
  Button button_2 (.out(button_2_out));
  Caminho_de_Dados caminho_de_dados_1 (
    .in_2(clock_out), .STO(logica_de_controle_1_wr_ram), .En_RAM(logica_de_controle_1_en_ram),
    .WR_ACC(logica_de_controle_1_wr_acc), .Sel_ULA(logica_de_controle_1_ula_demux2),
    .SEL_OP2(logica_de_controle_1_sel_op2), .out_10(out_1), .SEL_OP1(logica_de_controle_1_sel_op1),
    .clr_ram(button_2_out), .IR_OUT(caminho_de_controle_1_out_5));

  // Notes on the sheet:
  //   Reset
  //   Reset RAM
  //   Caminho de Dados
endmodule

module WR_RAM (
  input  [15:0] in_1,
  output EN_RAM
);

  Comparator #(.width(16)) comparator_1 (.a(in_1), .b(16'h1000), .eq(EN_RAM));  // open: gt, lt
endmodule

module EN_RAM (
  input  [15:0] in_1,
  output out_2
);

  wire comparator_1_eq, comparator_2_eq, comparator_3_eq, comparator_4_eq;

  Comparator #(.width(16)) comparator_1 (.a(in_1), .b(16'h1000), .eq(comparator_1_eq));  // open: gt, lt
  Comparator #(.width(16)) comparator_2 (.a(in_1), .b(16'h2000), .eq(comparator_2_eq));  // open: gt, lt
  Comparator #(.width(16)) comparator_3 (.a(in_1), .b(16'h4000), .eq(comparator_3_eq));  // open: gt, lt
  Comparator #(.width(16)) comparator_4 (.a(in_1), .b(16'h6000), .eq(comparator_4_eq));  // open: gt, lt
  or or_1 (out_2, comparator_1_eq, comparator_2_eq, comparator_3_eq, comparator_4_eq);
endmodule

module WR_ACC (
  input  [15:0] in_1,
  output out_2
);

  wire comparator_1_eq, comparator_2_eq, comparator_3_eq, comparator_4_eq, comparator_5_eq, comparator_6_eq;

  Comparator #(.width(16)) comparator_1 (.a(in_1), .b(16'h2000), .eq(comparator_1_eq));  // open: gt, lt
  Comparator #(.width(16)) comparator_2 (.a(in_1), .b(16'h3000), .eq(comparator_2_eq));  // open: gt, lt
  Comparator #(.width(16)) comparator_3 (.a(in_1), .b(16'h4000), .eq(comparator_3_eq));  // open: gt, lt
  Comparator #(.width(16)) comparator_4 (.a(in_1), .b(16'h5000), .eq(comparator_4_eq));  // open: gt, lt
  Comparator #(.width(16)) comparator_5 (.a(in_1), .b(16'h6000), .eq(comparator_5_eq));  // open: gt, lt
  Comparator #(.width(16)) comparator_6 (.a(in_1), .b(16'h7000), .eq(comparator_6_eq));  // open: gt, lt
  or or_1 (out_2, comparator_1_eq, comparator_2_eq, comparator_3_eq, comparator_4_eq, comparator_5_eq, comparator_6_eq);
endmodule

module SEL_OP1 (
  input  [15:0] in_1,
  output [1:0] out_2
);

  wire comparator_1_eq, comparator_2_eq, comparator_3_eq, comparator_4_eq, comparator_5_eq, or_1_out;

  Comparator #(.width(16)) comparator_1 (.a(in_1), .b(16'h4000), .eq(comparator_1_eq));  // open: gt, lt
  Comparator #(.width(16)) comparator_2 (.a(in_1), .b(16'h5000), .eq(comparator_2_eq));  // open: gt, lt
  Comparator #(.width(16)) comparator_3 (.a(in_1), .b(16'h6000), .eq(comparator_3_eq));  // open: gt, lt
  Comparator #(.width(16)) comparator_4 (.a(in_1), .b(16'h7000), .eq(comparator_4_eq));  // open: gt, lt
  Comparator #(.width(16)) comparator_5 (.a(in_1), .b(16'h3000), .eq(comparator_5_eq));  // open: gt, lt
  or or_1 (or_1_out, comparator_1_eq, comparator_2_eq, comparator_3_eq, comparator_4_eq);
  assign out_2 = {{1{or_1_out}}, comparator_5_eq};  // Bit_Extender bit_extender_1
endmodule

module SEL_OP2 (
  input  [15:0] in_1,
  output out_2
);

  wire comparator_1_eq, comparator_2_eq, comparator_3_eq;

  Comparator #(.width(16)) comparator_1 (.a(in_1), .b(16'h3000), .eq(comparator_1_eq));  // open: gt, lt
  Comparator #(.width(16)) comparator_2 (.a(in_1), .b(16'h5000), .eq(comparator_2_eq));  // open: gt, lt
  Comparator #(.width(16)) comparator_3 (.a(in_1), .b(16'h7000), .eq(comparator_3_eq));  // open: gt, lt
  or or_1 (out_2, comparator_1_eq, comparator_2_eq, comparator_3_eq);
endmodule

module EN_PC (
  input  [15:0] in_1,
  output EN_PC
);

  wire comparator_1_eq;

  Comparator #(.width(16)) comparator_1 (.a(in_1), .b({16{1'b0}}), .eq(comparator_1_eq));  // open: gt, lt
  not not_1 (EN_PC, comparator_1_eq);
endmodule

module DEMUX2 (
  input  [15:0] in_1,
  output out_2
);

  wire comparator_1_eq, comparator_2_eq;

  Comparator #(.width(16)) comparator_1 (.a(in_1), .b(16'h6000), .eq(comparator_1_eq));  // open: gt, lt
  Comparator #(.width(16)) comparator_2 (.a(in_1), .b(16'h7000), .eq(comparator_2_eq));  // open: gt, lt
  or or_1 (out_2, comparator_1_eq, comparator_2_eq);
endmodule

module Logica_de_Controle (
  input  [15:0] in_1,
  output WR_RAM,
  output EN_RAM,
  output WR_ACC,
  output [1:0] SEL_OP1,
  output SEL_OP2,
  output ULA_DEMUX2,
  output EN_PC
);

  EN_PC en_pc_1 (.in_1(in_1), .EN_PC(EN_PC));
  WR_RAM wr_ram_1 (.in_1(in_1), .EN_RAM(WR_RAM));
  EN_RAM en_ram_1 (.in_1(in_1), .out_2(EN_RAM));
  WR_ACC wr_acc_1 (.in_1(in_1), .out_2(WR_ACC));
  SEL_OP1 sel_op1_1 (.in_1(in_1), .out_2(SEL_OP1));
  SEL_OP2 sel_op2_1 (.in_1(in_1), .out_2(SEL_OP2));
  DEMUX2 demux2_1 (.in_1(in_1), .out_2(ULA_DEMUX2));

  // Notes on the sheet:
  //   As instruções chegam do IR e ativa alguma das opções abaixo
endmodule

module Caminho_de_Controle (
  input  Clock,
  input  En_PC,
  input  CLR,
  output [15:0] out_4,
  output [15:0] out_5
);

  wire [15:0] adder_1_out, and_1_out, PC_q, rom_1_data;

  assign and_1_out = PC_q & 16'hfff;  // AND_Gate and_1, 16 bits wide
  Adder #(.width(16)) adder_1 (.a(and_1_out), .b(16'h1), .out(adder_1_out));  // open: cin, cout
  Register #(.width(16)) PC (.D(adder_1_out), .en(En_PC), .Q(PC_q), .clk(Clock), .clr(CLR));
  ROM #(.addrWidth(16), .dataWidth(16)) rom_1 (.addr(PC_q), .data(rom_1_data), .sel(1'b1));
  Register #(.width(16)) IR (.D(rom_1_data), .en(1'b1), .Q(out_5), .clk(Clock), .clr(CLR));
  assign out_4 = out_5 & 16'hf000;  // AND_Gate and_2, 16 bits wide

  // Notes on the sheet:
  //   contents of rom_1 (hex, n*v repeats v):
  //   2000 4001 7001 1002 5002 1003
endmodule

module Caminho_de_Dados (
  input  [15:0] IR_OUT,
  input  in_2,
  input  STO,
  input  En_RAM,
  input  [1:0] SEL_OP1,
  input  WR_ACC,
  input  Sel_ULA,
  input  SEL_OP2,
  input  clr_ram,
  output [15:0] out_10
);

  wire [15:0] ACC_q, adder_1_out, and_1_out, demultiplexer_1_out0, demultiplexer_1_out1,
       demultiplexer_2_out0, demultiplexer_2_out1, multiplexer_1_out, multiplexer_2_out, ram_1_data,
       subtractor_1_out;

  RAM #(.addrWidth(16), .dataWidth(16), .bus("separate")) ram_1 (
    .addr(and_1_out), .din(ACC_q), .data(ram_1_data), .str(STO), .sel(En_RAM), .clk(in_2), .clr(clr_ram));  // open: ld
  Multiplexer #(.width(16), .enable("false")) multiplexer_1 (
    .in0(ram_1_data), .in1(and_1_out), .out(multiplexer_1_out), .sel(SEL_OP2));
  Demultiplexer #(.width(16), .enable("false")) demultiplexer_1 (
    .out0(demultiplexer_1_out0), .out1(demultiplexer_1_out1), .in(multiplexer_1_out), .sel(1'b1));
  assign and_1_out = IR_OUT & 16'hfff;  // AND_Gate and_1, 16 bits wide
  Adder #(.width(16)) adder_1 (
    .a(demultiplexer_2_out0), .b(demultiplexer_1_out0), .out(adder_1_out));  // open: cin, cout
  Multiplexer #(.select(2), .width(16), .enable("false")) multiplexer_2 (
    .in0(ram_1_data), .in1(and_1_out), .in2(out_10), .out(multiplexer_2_out), .sel(SEL_OP1));  // open: in3
  Register #(.width(16)) ACC (.D(multiplexer_2_out), .en(WR_ACC), .Q(ACC_q), .clk(in_2), .clr(clr_ram));
  Demultiplexer #(.width(16), .enable("false")) demultiplexer_2 (
    .out0(demultiplexer_2_out0), .out1(demultiplexer_2_out1), .in(ACC_q), .sel(Sel_ULA));
  Subtractor #(.width(16)) subtractor_1 (
    .a(demultiplexer_1_out1), .b(demultiplexer_2_out1), .out(subtractor_1_out));  // open: bin, bout
  Multiplexer #(.width(16), .enable("false")) multiplexer_3 (
    .in0(adder_1_out), .in1(subtractor_1_out), .out(out_10), .sel(1'b1));
endmodule
