// Logisim project TEMPLATE.circ as structural Verilog: 1 circuit, main circuit main
module main (
);

  wire not_1_out, not_2_out, not_3_out, not_4_out, undriven, undriven_2, undriven_3, undriven_4;

  not not_1 (not_1_out, undriven);
  not not_2 (not_2_out, undriven_2);
  not not_3 (not_3_out, undriven_3);
  not not_4 (not_4_out, undriven_4);
  // AND_Gate and_1 is placed but not wired
  // AND_Gate and_2 is placed but not wired
  // AND_Gate and_3 is placed but not wired
  // OR_Gate or_1 is placed but not wired

  // Notes on the sheet:
  //   A A'
  //   C C'
  //   B B'
  //   D D'
endmodule
